# Fritzing sketch interface audio morse (saved by Fritzing 0.9.10b)
circuit board: 5.56162cm x 4.3451cm
breadboards: 1

parts:
  U1 = 555 Timer [package="DIP8 [THT]"]
  R1 = Resistor [tolerance=±1% power=0.25 resistance=22k package=THT]
  C1 = Ceramic Capacitor [capacitance=100nF voltage=35V package="100 mil [THT, multilayer]"]
  C2 = Ceramic Capacitor [capacitance=100nF voltage=35V package="100 mil [THT, multilayer]"]
  Q1 = PNP-Transistor [package="TO92 [THT]"]
  Q2 = NPN-Transistor [package="TO92 [THT]"]
  R2 = Resistor [tolerance=±5% power=0.25 resistance=10k package=THT]
  R3 = Resistor [tolerance=±5% power=0.25 resistance=10k package=THT]
  Mod1 = Raspberry Pi Pico
  Composant1 = Breakout Board for Electret Microphone
  C3 = Ceramic Capacitor [capacitance=10nF voltage=35V package="100 mil [THT, multilayer]"]

nets:
  GND: U1.Ground, C1.1, C2.1, Q1.C, Q2.E, Mod1.pin_3, Mod1.pin_8, Mod1.pin_13, Mod1.pin_18, Mod1.pin_23, Mod1.pin_28, Mod1.pin_33, Mod1.pin_38, C3.0
  N1: U1.Trigger, Q1.B, Composant1.AUD, C3.1
  N2: U1.Output, R2.Pin_0
  N3: U1.Reset, U1.Vcc_Supply_Voltage, R1.Pin_0
  N4: U1.Control_Voltage, C1.0
  N5: U1.Threshold, U1.Discharge, R1.Pin_1, C2.0, Q1.E
  N6: Q2.B, R2.Pin_1
  N7: Q2.C, R3.Pin_1, Mod1.pin_10
  N8: R3.Pin_0, Mod1.pin_36

custom parts:
  Raspberry Pi Pico: Raspberry Pi Pico. Based around the RP2040 microcontroller the Pico is a low cost microcontroller device bringing Raspberry Pi quality, cost, and easy of use to the microcontroller space. Jan 2021, Split part in to two versions: tht (this one) and SMD. This one will drill holes for a .1 in header in pcb to allow plugging in the module as well as providing pads to solder the module to the top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
